# Fritzing sketch 3PinActiveBuzzer (saved by Fritzing 0.9.10b)
breadboards: 1

parts:
  Part1 = Arduino Mega ADK (Rev3)
  Mod2 = KY-012 Active Buzzer Module [package="Breakout board"]

nets:
  N1: Part1.GND, Mod2.-
  N2: Part1.D2_PWM, Mod2.S

custom parts:
  KY-012 Active Buzzer Module: Active Piezoelectric Buzzer Module KY-012, it produces single-tone sound when signal is high. (Special thanks to vanepp for fixing the PCB holes and other errors)
